// Logisim project Nano8v1.circ as structural Verilog
module ALU (
  input  [7:0] A,
  input  [7:0] B,
  input  [3:0] OP,
  input  CI,
  output [7:0] S,
  output CO
);

  wire ADD, adder_1_cout, AND_OP, demultiplexer_1_out9, demultiplexer_1_out10, demultiplexer_1_out11,
       demultiplexer_1_out12, demultiplexer_1_out13, demultiplexer_1_out14, demultiplexer_1_out15, LSL, LSR,
       NOT_OP, OR_OP, SUB, XOR_OP;
  wire [7:0] adder_1_out;

  Pull_Resistor pull_resistor_1 (.node(S));
  Pull_Resistor pull_resistor_2 (.node(CO));
  Demultiplexer #(.select(4)) demultiplexer_1 (
    .out1(ADD), .out2(SUB), .out3(AND_OP), .out4(OR_OP), .out5(NOT_OP), .out6(XOR_OP), .out7(LSL),
    .out8(LSR), .out9(demultiplexer_1_out9), .out10(demultiplexer_1_out10), .out11(demultiplexer_1_out11),
    .out12(demultiplexer_1_out12), .out13(demultiplexer_1_out13), .out14(demultiplexer_1_out14),
    .out15(demultiplexer_1_out15), .in(1'b1), .sel(OP));  // open: out0
  Adder adder_1 (.a(A), .b(B), .out(adder_1_out), .cin(CI), .cout(adder_1_cout));
  assign S = ADD ? adder_1_out : 8'bz;  // Controlled_Buffer controlled_buffer_1
  assign CO = ADD ? adder_1_cout : 1'bz;  // Controlled_Buffer controlled_buffer_2
endmodule

module CPU (
);

  wire AIN, AOUT, BIN, BOUT, CIN, CLK, COUT, demultiplexer_1_out4, demultiplexer_1_out5,
       demultiplexer_1_out6, demultiplexer_1_out7, demultiplexer_1_out8, demultiplexer_1_out9,
       demultiplexer_1_out10, demultiplexer_1_out11, demultiplexer_1_out12, demultiplexer_1_out13,
       demultiplexer_1_out14, demultiplexer_1_out15, demultiplexer_2_out4, demultiplexer_2_out5,
       demultiplexer_2_out6, demultiplexer_2_out7, demultiplexer_2_out8, demultiplexer_2_out9,
       demultiplexer_2_out10, demultiplexer_2_out11, demultiplexer_2_out12, demultiplexer_2_out13,
       demultiplexer_2_out14, demultiplexer_2_out15, dipswitch_2_p2, MAN, RES;
  wire [3:0] IN_C, OUT_C, undriven_2, undriven_3;
  wire [7:0] DATA, register_1_q, register_2_q, register_3_q, undriven;

  Clock clock_1 (.out(CLK));
  Register register_1 (.D(DATA), .en(AIN), .clk(CLK), .Q(register_1_q), .clr(RES));
  Register register_2 (.D(DATA), .en(BIN), .clk(CLK), .Q(register_2_q), .clr(RES));
  Register register_3 (.D(DATA), .en(CIN), .clk(CLK), .Q(register_3_q), .clr(RES));
  assign DATA = AOUT ? register_1_q : 8'bz;  // Controlled_Buffer controlled_buffer_1
  assign DATA = BOUT ? register_2_q : 8'bz;  // Controlled_Buffer controlled_buffer_2
  assign DATA = COUT ? register_3_q : 8'bz;  // Controlled_Buffer controlled_buffer_3
  // DipSwitch dipswitch_1: pin names not known
  // DipSwitch #(.number(2)) dipswitch_2: pin names not known; wires that end beside it: MAN, dipswitch_2_p2
  assign IN_C = dipswitch_2_p2 ? undriven_2 : 4'bz;  // Controlled_Buffer controlled_buffer_4
  // DipSwitch #(.number(4)) dipswitch_3: pin names not known
  assign OUT_C = dipswitch_2_p2 ? undriven_3 : 4'bz;  // Controlled_Buffer controlled_buffer_5
  // DipSwitch #(.number(4)) dipswitch_4: pin names not known
  assign DATA = MAN ? undriven : 8'bz;  // Controlled_Buffer controlled_buffer_6
  Pull_Resistor pull_resistor_1 (.node(DATA));
  Pull_Resistor pull_resistor_2 (.node(IN_C));
  Pull_Resistor pull_resistor_3 (.node(OUT_C));
  Demultiplexer #(.select(4)) demultiplexer_1 (
    .out1(AIN), .out2(BIN), .out3(CIN), .out4(demultiplexer_1_out4), .out5(demultiplexer_1_out5),
    .out6(demultiplexer_1_out6), .out7(demultiplexer_1_out7), .out8(demultiplexer_1_out8),
    .out9(demultiplexer_1_out9), .out10(demultiplexer_1_out10), .out11(demultiplexer_1_out11),
    .out12(demultiplexer_1_out12), .out13(demultiplexer_1_out13), .out14(demultiplexer_1_out14),
    .out15(demultiplexer_1_out15), .in(1'b1), .sel(IN_C));  // open: out0
  Demultiplexer #(.select(4)) demultiplexer_2 (
    .out1(AOUT), .out2(BOUT), .out3(COUT), .out4(demultiplexer_2_out4), .out5(demultiplexer_2_out5),
    .out6(demultiplexer_2_out6), .out7(demultiplexer_2_out7), .out8(demultiplexer_2_out8),
    .out9(demultiplexer_2_out9), .out10(demultiplexer_2_out10), .out11(demultiplexer_2_out11),
    .out12(demultiplexer_2_out12), .out13(demultiplexer_2_out13), .out14(demultiplexer_2_out14),
    .out15(demultiplexer_2_out15), .in(1'b1), .sel(OUT_C));  // open: out0

  // Notes on the sheet:
  //   Registers
  //   Manula Control
  //   Control Decoder
endmodule
